// Logisim project Labb 2.circ as structural Verilog: 2 circuits, main circuit main
module main (
  input  in_1,
  input  in_2,
  input  in_3,
  input  in_4,
  output out_5
);

  wire and_1_out, and_2_out, and_3_out, and_4_out, and_5_out, and_6_out, and_7_out, not_1_out, not_2_out,
       not_3_out, not_4_out;

  not not_1 (not_1_out, in_1);
  not not_2 (not_2_out, in_2);
  not not_3 (not_3_out, in_3);
  and and_1 (and_1_out, in_1, not_2_out, not_3_out, in_4);
  and and_2 (and_2_out, in_1, not_2_out, in_3, not_4_out);
  and and_3 (and_3_out, in_1, in_2, in_3, in_4);
  not not_4 (not_4_out, in_4);
  and and_4 (and_4_out, not_1_out, not_2_out, in_3, not_4_out);
  and and_5 (and_5_out, not_1_out, in_2, not_3_out, not_4_out);
  and and_6 (and_6_out, not_1_out, in_2, not_3_out, in_4);
  and and_7 (and_7_out, in_1, not_2_out, not_3_out, not_4_out);
  or or_1 (out_5, and_4_out, and_5_out, and_6_out, and_7_out, and_1_out, and_2_out, and_3_out);
endmodule

module New_labb2 (
  input  a,
  input  b,
  input  c,
  input  d,
  output x
);

  wire and_1_out, and_2_out, and_3_out, and_4_out, not_1_out, not_2_out, not_3_out, not_4_out, not_5_out,
       not_6_out;

  not not_1 (not_1_out, b);
  and and_1 (and_1_out, not_1_out, c, not_2_out);
  not not_2 (not_2_out, d);
  not not_3 (not_3_out, a);
  and and_2 (and_2_out, not_3_out, b, not_4_out);
  not not_4 (not_4_out, c);
  not not_5 (not_5_out, b);
  and and_3 (and_3_out, a, not_5_out, not_6_out);
  not not_6 (not_6_out, c);
  and and_4 (and_4_out, a, b, c, d);
  or or_1 (x, and_1_out, and_2_out, and_3_out, and_4_out);
endmodule
