// Logisim project labb3.circ as structural Verilog: 1 circuit, main circuit main
module main (
  input  [1:0] in_1,
  input  in_2,
  input  in_3,
  output out_4,
  output out_5,
  output out_6,
  output out_7
);

  wire clock_1_out, not_1_out, not_2_out, or_1_out, or_2_out, or_3_out;

  not not_1 (not_1_out, in_2);
  not not_2 (not_2_out, in_3);
  or or_1 (or_1_out, in_2, not_2_out);
  or or_2 (or_2_out, not_1_out, in_3);
  or or_3 (or_3_out, not_1_out, not_2_out);
  Multiplexer #(.select(2)) multiplexer_1 (
    .in0(in_3), .in1(in_3), .in2(or_1_out), .in3(not_1_out), .out(out_5), .sel(in_1));  // open: en
  Multiplexer #(.select(2)) multiplexer_2 (
    .in0(or_2_out), .in1(not_1_out), .in2(or_3_out), .in3(or_3_out), .out(out_6), .sel(in_1));  // open: en
  Clock clock_1 (.out(clock_1_out));
  D_Flip_Flop d_ff_1 (.clk(clock_1_out), .D(out_5), .Q(out_4));  // open: Qn, preset, en, reset
  D_Flip_Flop d_ff_2 (.clk(clock_1_out), .D(out_6), .Q(out_7));  // open: Qn, preset, en, reset
endmodule
